# Fritzing sketch MoistureServoProMini9V (saved by Fritzing 0.9.2b)
circuit board: 3.69603cm x 3.77562cm
breadboards: 1

parts:
  PART1 = SparkFun Soil Moisture Sensor [part_number=SEN-13322]
  VCC1 = Battery block 9V
  Part1 = Arduino Pro Mini v13
  LED1 = RGB LED (com. anode, rbg) [package="5 mm [THT]"]
  part = Resistor [tolerance=±5% resistance=330 package="1206 [SMD]"]
  part_2 = Resistor [tolerance=±5% resistance=330 package="1206 [SMD]"]
  part_3 = Resistor [tolerance=±5% resistance=330 package="1206 [SMD]"]

nets:
  VCC: PART1.VCC, Part1.VCC, LED1.common_anode
  GND: PART1.GND, VCC1.-, Part1.GND
  N1: PART1.SIG, Part1.A0
  N2: VCC1.+, Part1.RAW
  N3: Part1.D6_PWM, part.Pin_0
  N4: Part1.D5_PWM, part_2.Pin_0
  N5: Part1.D3_PWM, part_3.Pin_0
  N6: LED1.red_cathode, part_3.Pin_1
  N7: LED1.blue_cathode, part_2.Pin_1
  N8: LED1.green_cathode, part.Pin_1

custom parts:
  SparkFun Soil Moisture Sensor: The SparkFun Soil Moisture Sensor is a simple breakout for measuring the moisture in soil and similar materials.
